# Fritzing sketch simplebotpcb (saved by Fritzing 0.8.7b)
circuit board: 6.9215cm x 5.33756cm
breadboards: 1

parts:
  1 = Basic Servo
  2 = Basic Servo
  3 = Basic Servo
  4 = Basic Servo
  Nano = Arduino Nano (Rev3.0)
  Servo_Batt = Battery
  BT_(RX->) = female pin header, 6 pins [form="♀ (female)"]
  WiFI_(1->) = female pin header, 10 pins [form="♀ (female)"]
  Sonic_(+->) = female pin header, 4 pins [form="♀ (female)"]
  Uno = Arduino Uno (Rev3) - ICSP

nets:
  GND: 1.gnd, 2.gnd, 3.gnd, 4.gnd, Nano.GND, Servo_Batt.-, BT_(RX->).pin4, WiFI_(1->).pin1, Sonic_(+->).pin4, Uno.GND
  VCC: 1.vcc, 2.vcc, 3.vcc, 4.vcc, Servo_Batt.+
  N1: 1.pulse, Nano.D3, Uno.D3_PWM
  N2: 2.pulse, Nano.D4, Uno.D4
  N3: 3.pulse, Nano.D8, Uno.D8
  N4: 4.pulse, Nano.D9, Uno.D9_PWM
  N5: Nano.D1/TX, BT_(RX->).pin2, WiFI_(1->).pin5, Uno.D1/TX
  N6: Nano.D0/RX, BT_(RX->).pin3, WiFI_(1->).pin6, Uno.D0/RX
  N7: Nano.RESET, Uno.RESET
  N8: Nano.D2, Uno.D2
  N9: Nano.D5, Uno.D5_PWM
  N10: Nano.D6, Uno.D6_PWM
  N11: Nano.D7, Sonic_(+->).pin2, Sonic_(+->).pin3, Uno.D7
  N12: Nano.D10, Uno.D10_PWM/SS
  N13: Nano.D11/MOSI, Uno.ICSP_MOSI, Uno.D11_PWM/MOSI
  N14: Nano.D12/MISO, Uno.ICSP_MISO, Uno.D12/MISO
  VIN: Nano.VIN, Uno.VIN
  5V: Nano.5V, BT_(RX->).pin5, Sonic_(+->).pin1, Uno.5V
  3V3: Nano.3V3, WiFI_(1->).pin2, Uno.3V3
  N15: Nano.D13/SCK, Uno.ICSP_SCK, Uno.D13/SCK

notes:
  Servos
  +
  SimpleBot Shield V2.5
